# Fritzing sketch 32kRAM32kROM (saved by Fritzing 0.9.4)
circuit board: 11cm x 8cm
stripboards: 1

parts:
  Part1 = RC2014 bus connector [package=THT]
  U1 = SN74LS14N [package="DIP14 [THT]"]
  U2 = SN74LS32N [package="DIP14 [THT]"]
  AT28C1 = AT28C256 - 256K EEPROM [package="DIP (Dual Inline) [THT]"]
  IDT71256SA1 = IDT71256SA - 256K SRAM [part_number=IDT7164S package="DIP (Dual Inline) [THT]"]

nets:
  N1: Part1.A15, U1.6A, AT28C1.CE#
  N2: Part1.A14, AT28C1.A14, IDT71256SA1.A14
  N3: Part1.A13, AT28C1.A13, IDT71256SA1.A13
  N4: Part1.A12, AT28C1.A12, IDT71256SA1.A12
  N5: Part1.A11, AT28C1.A11, IDT71256SA1.A11
  N6: Part1.A10, AT28C1.A10, IDT71256SA1.A10
  N7: Part1.A9, AT28C1.A9, IDT71256SA1.A9
  N8: Part1.A8, AT28C1.A8, IDT71256SA1.A8
  N9: Part1.A7, AT28C1.A7, IDT71256SA1.A7
  N10: Part1.A6, AT28C1.A6, IDT71256SA1.A6
  N11: Part1.A5, AT28C1.A5, IDT71256SA1.A5
  N12: Part1.A4, AT28C1.A4, IDT71256SA1.A4
  N13: Part1.A3, AT28C1.A3, IDT71256SA1.A3
  N14: Part1.A2, AT28C1.A2, IDT71256SA1.A2
  N15: Part1.A1, AT28C1.A1, IDT71256SA1.A1
  N16: Part1.A0, AT28C1.A0, IDT71256SA1.A0
  GND: Part1.GND, U1.GND, U2.GND, AT28C1.GND, IDT71256SA1.GND
  VCC: Part1.5V, U1.VCC, U2.Vcc, AT28C1.WE#, AT28C1.VCC, IDT71256SA1.VCC
  N17: Part1.MRQ, U2.1B, U2.2A
  N18: Part1.WR, U2.1A
  N19: Part1.RD, U2.2B
  N20: Part1.D0, AT28C1.D0, IDT71256SA1.D0
  N21: Part1.D1, AT28C1.D1, IDT71256SA1.D1
  N22: Part1.D2, AT28C1.D2, IDT71256SA1.D2
  N23: Part1.D3, AT28C1.D3, IDT71256SA1.D3
  N24: Part1.D4, AT28C1.D4, IDT71256SA1.D4
  N25: Part1.D5, AT28C1.D5, IDT71256SA1.D5
  N26: Part1.D6, AT28C1.D6, IDT71256SA1.D6
  N27: Part1.D7, AT28C1.D7, IDT71256SA1.D7
  N28: U1.6Y, IDT71256SA1.CS#
  N29: U2.1Y, IDT71256SA1.WE#
  N30: U2.2Y, AT28C1.OE#, IDT71256SA1.OE#

custom parts:
  AT28C256 - 256K EEPROM: 256K (32K x 8) Paged Parallel EEPROM
  IDT71256SA - 256K SRAM: CMOS Static RAM 256K (32K x 8-Bit) Through-hole DIP
