# Fritzing sketch display (saved by Fritzing 0.9.4)
stripboards: 1

parts:
  J1 = female pin header, 7 pins [form="♀ (female)"]
  J2 = female pin header, 7 pins [form="♀ (female)"]
  J3 = female pin header, 7 pins [form="♀ (female)"]
  J4 = female pin header, 7 pins [form="♀ (female)"]
  J5 = female pin header, 7 pins [form="♀ (female)"]
  J6 = female pin header, 7 pins [form="♀ (female)"]
  J7 = female pin header, 7 pins [form="♀ (female)"]
  J8 = female pin header, 7 pins [form="♀ (female)"]
  J9 = female pin header, 7 pins [form="♀ (female)"]
  J10 = female pin header, 7 pins [form="♀ (female)"]
  J11 = female pin header, 7 pins [form="♀ (female)"]
  J12 = female pin header, 7 pins [form="♀ (female)"]
  J13 = female pin header, 7 pins [form="♀ (female)"]
  J14 = female pin header, 7 pins [form="♀ (female)"]
  J15 = female pin header, 7 pins [form="♀ (female)"]
  J16 = female pin header, 7 pins [form="♀ (female)"]
  Part1 = RC2014 bus connector [package=THT]
  74HC138N1 = 74HC138N [part_number=74HC138N package="DIP (Dual Inline) [THT]"]
  R1 = Resistor [tolerance=±5% resistance=10k package=THT]
  74HC541N1 = 74HC541N [part_number=74HC541N package="DIP (Dual Inline) [THT]"]
  D7 = Rectifier Diode [part_number=1N4001 package="Melf DO-213 AB [SMD]"]
  D8 = Rectifier Diode [part_number=1N4001 package="Melf DO-213 AB [SMD]"]
  D9 = Rectifier Diode [part_number=1N4001 package="Melf DO-213 AB [SMD]"]
  D10 = Rectifier Diode [part_number=1N4001 package="Melf DO-213 AB [SMD]"]
  D11 = Rectifier Diode [part_number=1N4001 package="Melf DO-213 AB [SMD]"]
  D12 = Rectifier Diode [part_number=1N4001 package="Melf DO-213 AB [SMD]"]

nets:
  VCC: J1.pin1, J2.pin1, J3.pin1, J4.pin1, J5.pin1, J6.pin1, J7.pin1, J8.pin1, J9.pin1, J10.pin1, J11.pin1, J12.pin1, J13.pin1, J14.pin1, J15.pin1, J16.pin1, Part1.5V, Part1.NC#39, 74HC138N1.VCC, 74HC541N1.VCC
  N1: J1.pin5, J3.pin5, 74HC138N1.Y3
  GND: J1.pin7, J2.pin7, J3.pin7, J4.pin7, J5.pin7, J6.pin7, J7.pin7, J8.pin7, J9.pin7, J10.pin7, J11.pin7, J12.pin7, J13.pin7, J14.pin7, J15.pin7, J16.pin7, Part1.GND, 74HC138N1.GND, R1.Pin_0, 74HC541N1.OE1#, 74HC541N1.GND, 74HC541N1.OE2#
  N2: J5.pin5, J7.pin5, 74HC138N1.Y2
  N3: J9.pin5, J11.pin5, 74HC138N1.Y1
  N4: J13.pin5, J15.pin5, 74HC138N1.Y0
  N5: Part1.A7, D11.anode
  N6: Part1.A6, D12.anode
  N7: Part1.A5, D8.anode
  N8: Part1.A4, D7.anode
  N9: Part1.A3, D9.anode
  N10: Part1.A2, D10.anode
  N11: Part1.A1, 74HC138N1.B
  N12: Part1.A0, 74HC138N1.A
  N13: Part1.M1, 74HC138N1.G1
  N14: Part1.WR, 74HC138N1.G2A#
  N15: Part1.IORQ, 74HC138N1.G2B#
  N16: Part1.D0, 74HC541N1.A1
  N17: Part1.D1, 74HC541N1.A2
  N18: Part1.D2, 74HC541N1.A3
  N19: Part1.D3, 74HC541N1.A4
  N20: Part1.D4, 74HC541N1.A5
  N21: Part1.D5, 74HC541N1.A6
  N22: Part1.D6, 74HC541N1.A7
  N23: Part1.D7, 74HC541N1.A8
  N24: 74HC138N1.C, R1.Pin_1, D7.cathode, D8.cathode, D9.cathode, D10.cathode, D11.cathode, D12.cathode

custom parts:
  74HC138N: 3 to 8 line Decoder/Demultiplexer
  74HC541N: Octal Buffers and Line Drivers With 3-State Outputs
